// Logisim project Projet_L2_Archi.circ as structural Verilog: 16 circuits, main circuit main
module Decodeur3 (
  input  F0,
  input  F1,
  input  F2,
  output S_0,
  output S_1,
  output S_2,
  output S_3,
  output S_4,
  output S_5,
  output S_6,
  output S_7
);

  wire not_1_out, not_2_out, not_3_out;

  not not_1 (not_1_out, F0);
  not not_2 (not_2_out, F1);
  not not_3 (not_3_out, F2);
  and and_1 (S_0, not_3_out, not_2_out, not_1_out);
  and and_2 (S_1, F0, not_2_out, not_3_out);
  and and_3 (S_2, not_1_out, F1, not_3_out);
  and and_4 (S_3, F0, F1, not_3_out);
  and and_5 (S_4, not_1_out, not_2_out, F2);
  and and_6 (S_5, F0, not_2_out, F2);
  and and_7 (S_6, not_1_out, F1, F2);
  and and_8 (S_7, F0, F1, F2);
endmodule

module FullAdder (
  input  Ret_In,
  input  A,
  input  B,
  output S,
  output Ret_Out
);

  wire and_1_out, and_2_out, xor_1_out;

  and and_1 (and_1_out, A, B);
  or or_1 (Ret_Out, and_1_out, and_2_out);
  xor xor_1 (xor_1_out, A, B);
  and and_2 (and_2_out, xor_1_out, Ret_In);
  xor xor_2 (S, Ret_In, xor_1_out);
endmodule

module FullAdder4 (
  input  Ret_In,
  input  [3:0] A,
  input  [3:0] B,
  output [3:0] S,
  output Ret_Out
);

  wire fulladder_1_ret_out, fulladder_2_ret_out, fulladder_3_ret_out;

  FullAdder fulladder_1 (.A(A[0]), .B(B[0]), .S(S[0]), .Ret_In(Ret_In), .Ret_Out(fulladder_1_ret_out));
  FullAdder fulladder_2 (.A(A[1]), .B(B[1]), .S(S[1]), .Ret_In(fulladder_1_ret_out), .Ret_Out(fulladder_2_ret_out));
  FullAdder fulladder_3 (.A(A[2]), .B(B[2]), .S(S[2]), .Ret_In(fulladder_2_ret_out), .Ret_Out(fulladder_3_ret_out));
  FullAdder fulladder_4 (.A(A[3]), .B(B[3]), .S(S[3]), .Ret_In(fulladder_3_ret_out), .Ret_Out(Ret_Out));
endmodule

module Substractor4 (
  input  [3:0] A,
  input  [3:0] B,
  output [3:0] S
);

  wire fulladder_1_ret_out, fulladder_2_ret_out, fulladder_3_ret_out;
  wire [3:0] not_1_out;

  assign not_1_out = ~B;  // NOT_Gate not_1, 4 bits wide
  FullAdder fulladder_1 (.A(A[0]), .B(not_1_out[0]), .S(S[0]), .Ret_In(1'b1), .Ret_Out(fulladder_1_ret_out));
  FullAdder fulladder_2 (
    .A(A[1]), .B(not_1_out[1]), .S(S[1]), .Ret_In(fulladder_1_ret_out), .Ret_Out(fulladder_2_ret_out));
  FullAdder fulladder_3 (
    .A(A[2]), .B(not_1_out[2]), .S(S[2]), .Ret_In(fulladder_2_ret_out), .Ret_Out(fulladder_3_ret_out));
  FullAdder fulladder_4 (.A(A[3]), .B(not_1_out[3]), .S(S[3]), .Ret_In(fulladder_3_ret_out));  // open: Ret_Out
endmodule

module MUX2_1 (
  input  A,
  input  B,
  input  Sel,
  output Out
);

  wire and_1_out, and_2_out, not_1_out;

  not not_1 (not_1_out, Sel);
  and and_1 (and_1_out, A, Sel);
  and and_2 (and_2_out, B, not_1_out);
  or or_1 (Out, and_1_out, and_2_out);
endmodule

module Mux2_4 (
  input  [3:0] In_1,
  input  [3:0] In_2,
  input  Sel,
  output [3:0] Out
);

  MUX2_1 mux2_1_1 (.A(In_2[0]), .B(In_1[0]), .Sel(Sel), .Out(Out[0]));
  MUX2_1 mux2_1_2 (.A(In_2[1]), .B(In_1[1]), .Sel(Sel), .Out(Out[1]));
  MUX2_1 mux2_1_3 (.A(In_2[2]), .B(In_1[2]), .Sel(Sel), .Out(Out[2]));
  MUX2_1 mux2_1_4 (.A(In_2[3]), .B(In_1[3]), .Sel(Sel), .Out(Out[3]));
endmodule

module \Unité_logique  (
  input  A,
  input  B,
  output AorB,
  output A_B,
  output NotB
);

  not not_1 (NotB, B);
  or or_1 (AorB, A, B);
  and and_1 (A_B, A, B);
endmodule

module \Unité_logique_4  (
  input  [3:0] A,
  input  [3:0] B,
  output [3:0] Out_AorB,
  output [3:0] Out_A_B,
  output [3:0] Out_NotB
);

  \Unité_logique  \unité_logique_1  (.A(A[3]), .B(B[3]), .AorB(Out_AorB[3]), .A_B(Out_A_B[3]), .NotB(Out_NotB[3]));
  \Unité_logique  \unité_logique_2  (.A(A[2]), .B(B[2]), .AorB(Out_AorB[2]), .A_B(Out_A_B[2]), .NotB(Out_NotB[2]));
  \Unité_logique  \unité_logique_3  (.A(A[1]), .B(B[1]), .AorB(Out_AorB[1]), .A_B(Out_A_B[1]), .NotB(Out_NotB[1]));
  \Unité_logique  \unité_logique_4  (.A(A[0]), .B(B[0]), .AorB(Out_AorB[0]), .A_B(Out_A_B[0]), .NotB(Out_NotB[0]));
endmodule

module ALU_4 (
  input  [3:0] A,
  input  [3:0] B,
  input  [2:0] Sel,
  output [3:0] S,
  output Z,
  output Ret_Out
);

  wire and_1_out, and_2_out, and_3_out, and_4_out, and_5_out, and_7_out, decodeur3_1_s_0, decodeur3_1_s_1,
       decodeur3_1_s_2, decodeur3_1_s_3, decodeur3_1_s_4, fulladder4_1_ret_out, not_1_out, not_2_out,
       not_3_out, not_4_out, not_5_out;
  wire [3:0] controlled_buffer_4_out, controlled_buffer_5_out, controlled_buffer_6_out, fulladder4_1_s,
       pull_resistor_2_node, pull_resistor_3_node, substractor4_1_s, \unité_logique_4_1_out_a_b ,
       \unité_logique_4_1_out_aorb , \unité_logique_4_1_out_notb ;

  Decodeur3 decodeur3_1 (
    .F0(Sel[0]), .F1(Sel[1]), .F2(Sel[2]), .S_0(decodeur3_1_s_0), .S_1(decodeur3_1_s_1),
    .S_2(decodeur3_1_s_2), .S_3(decodeur3_1_s_3), .S_4(decodeur3_1_s_4));  // open: S_5, S_6, S_7
  \Unité_logique_4  \unité_logique_4_1  (
    .Out_A_B(\unité_logique_4_1_out_a_b ), .Out_NotB(\unité_logique_4_1_out_notb ), .A(A), .B(B),
    .Out_AorB(\unité_logique_4_1_out_aorb ));
  Substractor4 substractor4_1 (.S(substractor4_1_s), .A(A), .B(B));
  assign Ret_Out = decodeur3_1_s_0 ? fulladder4_1_ret_out : 1'bz;  // Controlled_Buffer controlled_buffer_1
  Pull_Resistor pull_resistor_1 (.node(Ret_Out));
  FullAdder4 fulladder4_1 (.S(fulladder4_1_s), .Ret_In(1'b0), .A(A), .B(B), .Ret_Out(fulladder4_1_ret_out));
  Pull_Resistor pull_resistor_2 (.node(pull_resistor_2_node));
  assign pull_resistor_2_node = decodeur3_1_s_0 ? fulladder4_1_s : 4'bz;  // Controlled_Buffer controlled_buffer_2
  Pull_Resistor pull_resistor_3 (.node(pull_resistor_3_node));
  assign pull_resistor_3_node = decodeur3_1_s_1 ? \unité_logique_4_1_out_aorb  : 4'bz;  // Controlled_Buffer controlled_buffer_3
  assign controlled_buffer_4_out = decodeur3_1_s_2 ? \unité_logique_4_1_out_a_b  : 4'bz;  // Controlled_Buffer controlled_buffer_4
  Pull_Resistor pull_resistor_4 (.node(controlled_buffer_4_out));
  assign controlled_buffer_5_out = decodeur3_1_s_3 ? \unité_logique_4_1_out_notb  : 4'bz;  // Controlled_Buffer controlled_buffer_5
  Pull_Resistor pull_resistor_5 (.node(controlled_buffer_5_out));
  assign controlled_buffer_6_out = decodeur3_1_s_4 ? substractor4_1_s : 4'bz;  // Controlled_Buffer controlled_buffer_6
  Pull_Resistor pull_resistor_6 (.node(controlled_buffer_6_out));
  assign S = pull_resistor_2_node | pull_resistor_3_node | controlled_buffer_4_out | controlled_buffer_5_out | controlled_buffer_6_out;  // OR_Gate or_1, 4 bits wide
  not not_1 (not_1_out, S[0]);
  not not_2 (not_2_out, S[1]);
  not not_3 (not_3_out, S[2]);
  not not_4 (not_4_out, S[3]);
  not not_5 (not_5_out, 1'b0);
  and and_1 (and_1_out, not_5_out, not_1_out);
  and and_2 (and_2_out, not_2_out, not_5_out);
  and and_3 (and_3_out, not_5_out, not_3_out);
  and and_4 (and_4_out, not_4_out, not_5_out);
  and and_5 (and_5_out, and_1_out, and_2_out);
  and and_6 (Z, and_5_out, and_7_out);
  and and_7 (and_7_out, and_3_out, and_4_out);
endmodule

module RegistreGeneral4 (
  input  Clock,
  input  [3:0] Ent_In,
  input  wA,
  input  Reset,
  input  R_2,
  input  R_1,
  output [3:0] Out_1,
  output [3:0] Out_2
);

  wire controlled_buffer_1_out, controlled_buffer_2_out, controlled_buffer_3_out, controlled_buffer_4_out,
       d_ff_1_q, d_ff_2_q, d_ff_3_q, d_ff_4_q;

  assign controlled_buffer_1_out = wA ? Ent_In[3] : 1'bz;  // Controlled_Buffer controlled_buffer_1
  assign controlled_buffer_2_out = wA ? Ent_In[2] : 1'bz;  // Controlled_Buffer controlled_buffer_2
  assign controlled_buffer_3_out = wA ? Ent_In[1] : 1'bz;  // Controlled_Buffer controlled_buffer_3
  assign controlled_buffer_4_out = wA ? Ent_In[0] : 1'bz;  // Controlled_Buffer controlled_buffer_4
  D_Flip_Flop d_ff_1 (.clk(Clock), .D(controlled_buffer_4_out), .Q(d_ff_1_q), .reset(Reset));  // open: Qn, preset, en
  D_Flip_Flop d_ff_2 (.clk(Clock), .D(controlled_buffer_3_out), .Q(d_ff_2_q), .reset(Reset));  // open: Qn, preset, en
  D_Flip_Flop d_ff_3 (.clk(Clock), .D(controlled_buffer_2_out), .Q(d_ff_3_q), .reset(Reset));  // open: Qn, preset, en
  D_Flip_Flop d_ff_4 (.clk(Clock), .D(controlled_buffer_1_out), .Q(d_ff_4_q), .reset(Reset));  // open: Qn, preset, en
  assign Out_2[0] = R_2 ? d_ff_1_q : 1'bz;  // Controlled_Buffer controlled_buffer_5
  assign Out_2[1] = R_2 ? d_ff_2_q : 1'bz;  // Controlled_Buffer controlled_buffer_6
  assign Out_1[0] = R_1 ? d_ff_1_q : 1'bz;  // Controlled_Buffer controlled_buffer_7
  assign Out_1[1] = R_1 ? d_ff_2_q : 1'bz;  // Controlled_Buffer controlled_buffer_8
  assign Out_2[2] = R_2 ? d_ff_3_q : 1'bz;  // Controlled_Buffer controlled_buffer_9
  assign Out_2[3] = R_2 ? d_ff_4_q : 1'bz;  // Controlled_Buffer controlled_buffer_10
  assign Out_1[2] = R_1 ? d_ff_3_q : 1'bz;  // Controlled_Buffer controlled_buffer_11
  assign Out_1[3] = R_1 ? d_ff_4_q : 1'bz;  // Controlled_Buffer controlled_buffer_12
endmodule

module RegistreIntsruction12 (
  input  Clock,
  input  [11:0] Ent_In,
  input  R_O2,
  input  R_O1,
  input  Write,
  input  Reset,
  output [11:0] Out_1,
  output [11:0] Out_2
);

  wire controlled_buffer_1_out, controlled_buffer_2_out, controlled_buffer_3_out, controlled_buffer_4_out,
       controlled_buffer_5_out, controlled_buffer_6_out, controlled_buffer_7_out, controlled_buffer_8_out,
       controlled_buffer_9_out, controlled_buffer_10_out, controlled_buffer_11_out, controlled_buffer_12_out,
       d_ff_1_q, d_ff_2_q, d_ff_3_q, d_ff_4_q, d_ff_5_q, d_ff_6_q, d_ff_7_q, d_ff_8_q, d_ff_9_q, d_ff_10_q,
       d_ff_11_q, d_ff_12_q;

  assign controlled_buffer_1_out = Write ? Ent_In[11] : 1'bz;  // Controlled_Buffer controlled_buffer_1
  assign controlled_buffer_2_out = Write ? Ent_In[9] : 1'bz;  // Controlled_Buffer controlled_buffer_2
  assign controlled_buffer_3_out = Write ? Ent_In[10] : 1'bz;  // Controlled_Buffer controlled_buffer_3
  assign controlled_buffer_4_out = Write ? Ent_In[7] : 1'bz;  // Controlled_Buffer controlled_buffer_4
  assign controlled_buffer_5_out = Write ? Ent_In[8] : 1'bz;  // Controlled_Buffer controlled_buffer_5
  assign controlled_buffer_6_out = Write ? Ent_In[4] : 1'bz;  // Controlled_Buffer controlled_buffer_6
  assign controlled_buffer_7_out = Write ? Ent_In[5] : 1'bz;  // Controlled_Buffer controlled_buffer_7
  assign controlled_buffer_8_out = Write ? Ent_In[6] : 1'bz;  // Controlled_Buffer controlled_buffer_8
  assign controlled_buffer_9_out = Write ? Ent_In[2] : 1'bz;  // Controlled_Buffer controlled_buffer_9
  assign controlled_buffer_10_out = Write ? Ent_In[3] : 1'bz;  // Controlled_Buffer controlled_buffer_10
  assign controlled_buffer_11_out = Write ? Ent_In[0] : 1'bz;  // Controlled_Buffer controlled_buffer_11
  assign controlled_buffer_12_out = Write ? Ent_In[1] : 1'bz;  // Controlled_Buffer controlled_buffer_12
  D_Flip_Flop d_ff_1 (.clk(Clock), .D(controlled_buffer_11_out), .Q(d_ff_1_q), .reset(Reset));  // open: Qn, preset, en
  D_Flip_Flop d_ff_2 (.clk(Clock), .D(controlled_buffer_12_out), .Q(d_ff_2_q), .reset(Reset));  // open: Qn, preset, en
  D_Flip_Flop d_ff_3 (.clk(Clock), .D(controlled_buffer_9_out), .Q(d_ff_3_q), .reset(Reset));  // open: Qn, preset, en
  D_Flip_Flop d_ff_4 (.clk(Clock), .D(controlled_buffer_10_out), .Q(d_ff_4_q), .reset(Reset));  // open: Qn, preset, en
  D_Flip_Flop d_ff_5 (.clk(Clock), .D(controlled_buffer_6_out), .Q(d_ff_5_q), .reset(Reset));  // open: Qn, preset, en
  D_Flip_Flop d_ff_6 (.clk(Clock), .D(controlled_buffer_7_out), .Q(d_ff_6_q), .reset(Reset));  // open: Qn, preset, en
  D_Flip_Flop d_ff_7 (.clk(Clock), .D(controlled_buffer_8_out), .Q(d_ff_7_q), .reset(Reset));  // open: Qn, preset, en
  D_Flip_Flop d_ff_8 (.clk(Clock), .D(controlled_buffer_4_out), .Q(d_ff_8_q), .reset(Reset));  // open: Qn, preset, en
  D_Flip_Flop d_ff_9 (.clk(Clock), .D(controlled_buffer_5_out), .Q(d_ff_9_q), .reset(Reset));  // open: Qn, preset, en
  D_Flip_Flop d_ff_10 (.clk(Clock), .D(controlled_buffer_2_out), .Q(d_ff_10_q), .reset(Reset));  // open: Qn, preset, en
  D_Flip_Flop d_ff_11 (.clk(Clock), .D(controlled_buffer_3_out), .Q(d_ff_11_q), .reset(Reset));  // open: Qn, preset, en
  D_Flip_Flop d_ff_12 (.clk(Clock), .D(controlled_buffer_1_out), .Q(d_ff_12_q), .reset(Reset));  // open: Qn, preset, en
  assign Out_2[0] = R_O2 ? d_ff_1_q : 1'bz;  // Controlled_Buffer controlled_buffer_13
  assign Out_1[0] = R_O1 ? d_ff_1_q : 1'bz;  // Controlled_Buffer controlled_buffer_14
  assign Out_1[1] = R_O1 ? d_ff_2_q : 1'bz;  // Controlled_Buffer controlled_buffer_15
  assign Out_2[1] = R_O2 ? d_ff_2_q : 1'bz;  // Controlled_Buffer controlled_buffer_16
  assign Out_2[2] = R_O2 ? d_ff_3_q : 1'bz;  // Controlled_Buffer controlled_buffer_17
  assign Out_2[3] = R_O2 ? d_ff_4_q : 1'bz;  // Controlled_Buffer controlled_buffer_18
  assign Out_1[2] = R_O1 ? d_ff_3_q : 1'bz;  // Controlled_Buffer controlled_buffer_19
  assign Out_1[3] = R_O1 ? d_ff_4_q : 1'bz;  // Controlled_Buffer controlled_buffer_20
  assign Out_1[4] = R_O1 ? d_ff_5_q : 1'bz;  // Controlled_Buffer controlled_buffer_21
  assign Out_2[4] = R_O2 ? d_ff_5_q : 1'bz;  // Controlled_Buffer controlled_buffer_22
  assign Out_2[5] = R_O2 ? d_ff_6_q : 1'bz;  // Controlled_Buffer controlled_buffer_23
  assign Out_2[6] = R_O2 ? d_ff_7_q : 1'bz;  // Controlled_Buffer controlled_buffer_24
  assign Out_1[5] = R_O1 ? d_ff_6_q : 1'bz;  // Controlled_Buffer controlled_buffer_25
  assign Out_1[6] = R_O1 ? d_ff_7_q : 1'bz;  // Controlled_Buffer controlled_buffer_26
  assign Out_1[7] = R_O1 ? d_ff_8_q : 1'bz;  // Controlled_Buffer controlled_buffer_27
  assign Out_2[7] = R_O2 ? d_ff_8_q : 1'bz;  // Controlled_Buffer controlled_buffer_28
  assign Out_2[8] = R_O2 ? d_ff_9_q : 1'bz;  // Controlled_Buffer controlled_buffer_29
  assign Out_1[8] = R_O1 ? d_ff_9_q : 1'bz;  // Controlled_Buffer controlled_buffer_30
  assign Out_1[9] = R_O1 ? d_ff_10_q : 1'bz;  // Controlled_Buffer controlled_buffer_31
  assign Out_2[9] = R_O2 ? d_ff_10_q : 1'bz;  // Controlled_Buffer controlled_buffer_32
  assign Out_2[10] = R_O2 ? d_ff_11_q : 1'bz;  // Controlled_Buffer controlled_buffer_33
  assign Out_2[11] = R_O2 ? d_ff_12_q : 1'bz;  // Controlled_Buffer controlled_buffer_34
  assign Out_1[10] = R_O1 ? d_ff_11_q : 1'bz;  // Controlled_Buffer controlled_buffer_35
  assign Out_1[11] = R_O1 ? d_ff_12_q : 1'bz;  // Controlled_Buffer controlled_buffer_36
endmodule

module Banc_De_Registre (
  input  [3:0] Ent_In,
  input  Clock,
  input  Reset,
  input  W_A,
  input  W_B,
  input  W_C,
  input  W_D,
  input  R_A1,
  input  R_B1,
  input  R_C1,
  input  R_D1,
  input  R_A2,
  input  R_B2,
  input  R_C2,
  input  R_D2,
  output [3:0] Out_1,
  output [3:0] Out_2
);

  wire [3:0] registregeneral4_1_out_1, registregeneral4_1_out_2;

  RegistreGeneral4 registregeneral4_1 (
    .Ent_In(Ent_In), .Out_1(registregeneral4_1_out_1), .Out_2(registregeneral4_1_out_2), .Clock(Clock),
    .wA(W_A), .Reset(Reset), .R_2(R_A2), .R_1(R_A1));
  RegistreGeneral4 registregeneral4_2 (
    .Ent_In(Ent_In), .Out_1(registregeneral4_1_out_1), .Out_2(registregeneral4_1_out_2), .Clock(Clock),
    .wA(W_B), .Reset(Reset), .R_2(R_B2), .R_1(R_B1));
  RegistreGeneral4 registregeneral4_3 (
    .Ent_In(Ent_In), .Out_1(registregeneral4_1_out_1), .Out_2(registregeneral4_1_out_2), .Clock(Clock),
    .wA(W_C), .Reset(Reset), .R_2(R_C2), .R_1(R_C1));
  RegistreGeneral4 registregeneral4_4 (
    .Ent_In(Ent_In), .Out_1(registregeneral4_1_out_1), .Out_2(registregeneral4_1_out_2), .Clock(Clock),
    .wA(W_D), .Reset(Reset), .R_2(R_D2), .R_1(R_D1));
  Pull_Resistor pull_resistor_1 (.node(registregeneral4_1_out_1));
  Pull_Resistor pull_resistor_2 (.node(registregeneral4_1_out_2));
  assign Out_1 = registregeneral4_1_out_1 | registregeneral4_1_out_1 | registregeneral4_1_out_1 | registregeneral4_1_out_1;  // OR_Gate or_1, 4 bits wide
  assign Out_2 = registregeneral4_1_out_2 | registregeneral4_1_out_2 | registregeneral4_1_out_2 | registregeneral4_1_out_2;  // OR_Gate or_2, 4 bits wide
endmodule

module Unite_Adressage (
  input  Clock,
  input  [3:0] PC_In,
  input  W_PC,
  input  [3:0] AD_In,
  input  W_AD,
  input  Reset,
  output [3:0] PC_Out,
  output [3:0] AD_Out
);

  wire not_1_out;

  not not_1 (not_1_out, Clock);
  RegistreGeneral4 registregeneral4_1 (
    .Ent_In(PC_In), .Out_1(PC_Out), .Clock(Clock), .wA(W_PC), .Reset(Reset), .R_2(1'b0), .R_1(1'b1));  // open: Out_2
  RegistreGeneral4 registregeneral4_2 (
    .Ent_In(AD_In), .Out_1(AD_Out), .Clock(not_1_out), .wA(W_AD), .Reset(Reset), .R_2(1'b0), .R_1(1'b1));  // open: Out_2
endmodule

module Instruction_decodeur (
  input  [3:0] Input,
  output W_PC,
  output Fetch,
  output S_2,
  output S_1,
  output S_0,
  output Read,
  output Write,
  output W_AD
);

  wire not_1_out, not_2_out, not_3_out, not_4_out, not_5_out, not_6_out, not_7_out, not_8_out, not_9_out,
       not_10_out, not_11_out, not_12_out;

  not not_1 (not_1_out, Input[1]);
  not not_2 (not_2_out, Input[3]);
  not not_3 (not_3_out, Input[2]);
  not not_4 (not_4_out, Input[3]);
  not not_5 (not_5_out, Input[2]);
  not not_6 (not_6_out, Input[3]);
  not not_7 (not_7_out, Input[0]);
  not not_8 (not_8_out, Input[1]);
  not not_9 (not_9_out, Input[3]);
  not not_10 (not_10_out, Input[0]);
  not not_11 (not_11_out, Input[1]);
  not not_12 (not_12_out, Input[2]);
  and and_1 (S_2, Input[0], not_1_out, Input[2], not_2_out);
  and and_2 (S_1, Input[1], not_3_out, not_4_out);
  and and_3 (S_0, Input[0], not_5_out, not_6_out);
  and and_4 (Read, not_7_out, not_8_out, Input[2], not_9_out);
  and and_5 (Write, not_10_out, not_11_out, not_12_out, Input[3]);
  or or_1 (W_AD, Read, Write);

  assign Fetch = 1'b1;
  assign W_PC = 1'b1;
endmodule

module \Unité_de_controle  (
  input  [11:0] Instruction,
  input  Clk,
  input  [3:0] PC_In,
  input  Reset,
  output WB,
  output WD,
  output RA2,
  output RB2,
  output RC2,
  output RD2,
  output WA,
  output WC,
  output RA1,
  output RB1,
  output RC1,
  output RD1,
  output [3:0] AD_Out,
  output Ext2,
  output Ext1,
  output F0,
  output F1,
  output F2,
  output Load,
  output Store,
  output Fetch,
  output W_PC,
  output W_AD,
  output [3:0] PC_Out
);

  wire decodeur3_1_s_4, decodeur3_1_s_5, decodeur3_1_s_6, decodeur3_1_s_7, decodeur3_2_s_0, decodeur3_2_s_1,
       decodeur3_2_s_2, decodeur3_2_s_3;
  wire [3:0] fulladder4_1_s;
  wire [11:6] registreintsruction12_1_out_1;

  Decodeur3 decodeur3_1 (
    .F0(registreintsruction12_1_out_1[6]), .F1(registreintsruction12_1_out_1[7]), .F2(Store), .S_0(WA),
    .S_1(WB), .S_2(WC), .S_3(WD), .S_4(decodeur3_1_s_4), .S_5(decodeur3_1_s_5), .S_6(decodeur3_1_s_6),
    .S_7(decodeur3_1_s_7));
  RegistreIntsruction12 registreintsruction12_1 (
    .Out_1({registreintsruction12_1_out_1, AD_Out, Ext2, Ext1}), .Ent_In(Instruction), .Clock(Clk),
    .Write(1'b1), .Reset(1'b0), .R_O2(1'b0), .R_O1(1'b1));  // open: Out_2
  FullAdder4 fulladder4_1 (.S(fulladder4_1_s), .Ret_In(1'b0), .A(PC_In), .B(4'b0001));  // open: Ret_Out
  or or_1 (RA1, decodeur3_1_s_4, decodeur3_2_s_0);
  Mux2_4 mux2_4_1 (.Out(PC_Out), .In_1(fulladder4_1_s), .In_2(4'b0000), .Sel(Reset));
  or or_2 (RB1, decodeur3_1_s_5, decodeur3_2_s_1);
  Decodeur3 decodeur3_2 (
    .F0(AD_Out[2]), .F1(AD_Out[3]), .F2(W_AD), .S_0(decodeur3_2_s_0), .S_1(decodeur3_2_s_1),
    .S_2(decodeur3_2_s_2), .S_3(decodeur3_2_s_3));  // open: S_4, S_5, S_6, S_7
  // Probe on registreintsruction12_1_out_1[11:8]
  or or_3 (RC1, decodeur3_1_s_6, decodeur3_2_s_2);
  or or_4 (RD1, decodeur3_1_s_7, decodeur3_2_s_3);
  Instruction_decodeur instruction_decodeur_1 (
    .Input(registreintsruction12_1_out_1[11:8]), .W_PC(W_PC), .Fetch(Fetch), .S_2(F2), .S_1(F1), .S_0(F0),
    .Read(Load), .Write(Store), .W_AD(W_AD));
  Decodeur3 decodeur3_3 (
    .F0(AD_Out[0]), .F1(AD_Out[1]), .F2(W_AD), .S_0(RA2), .S_1(RB2), .S_2(RC2), .S_3(RD2));  // open: S_4, S_5, S_6, S_7
endmodule

module main (
  input  Reset,
  output Z_Out__1_si_Soustraction_0__0_sinon,
  output Ret_Out
);

  wire Clk_out, \unité_de_controle_1_fetch , \unité_de_controle_1_load , \unité_de_controle_1_ra1 ,
       \unité_de_controle_1_ra2 , \unité_de_controle_1_rb1 , \unité_de_controle_1_rb2 ,
       \unité_de_controle_1_rc1 , \unité_de_controle_1_rc2 , \unité_de_controle_1_rd1 ,
       \unité_de_controle_1_rd2 , \unité_de_controle_1_store , \unité_de_controle_1_w_ad ,
       \unité_de_controle_1_w_pc , \unité_de_controle_1_wa , \unité_de_controle_1_wb ,
       \unité_de_controle_1_wc , \unité_de_controle_1_wd ;
  wire [2:0] \unité_de_controle_1_f0 ;
  wire [3:0] banc_de_registre_1_out_1, banc_de_registre_1_out_2, mux2_4_1_out, pull_resistor_1_node,
       pull_resistor_2_node, unite_adressage_1_ad_out, unite_adressage_1_pc_out,
       \unité_de_controle_1_ad_out , \unité_de_controle_1_pc_out ;
  wire [11:0] rom_1_data;

  // Probe on rom_1_data
  Pull_Resistor pull_resistor_1 (.node(pull_resistor_1_node));
  Pull_Resistor pull_resistor_2 (.node(pull_resistor_2_node));
  // Probe on mux2_4_1_out
  Mux2_4 mux2_4_1 (
    .Out(mux2_4_1_out), .In_1(pull_resistor_1_node), .In_2(pull_resistor_2_node),
    .Sel(\unité_de_controle_1_load ));
  Clock Clk (.out(Clk_out));
  Banc_De_Registre banc_de_registre_1 (
    .W_A(\unité_de_controle_1_wa ), .W_B(\unité_de_controle_1_wb ), .W_C(\unité_de_controle_1_wc ),
    .W_D(\unité_de_controle_1_wd ), .Out_1(banc_de_registre_1_out_1), .Out_2(banc_de_registre_1_out_2),
    .Ent_In(mux2_4_1_out), .Clock(Clk_out), .Reset(Reset), .R_A1(\unité_de_controle_1_ra1 ),
    .R_B1(\unité_de_controle_1_rb1 ), .R_C1(\unité_de_controle_1_rc1 ), .R_D1(\unité_de_controle_1_rd1 ),
    .R_A2(\unité_de_controle_1_ra2 ), .R_B2(\unité_de_controle_1_rb2 ), .R_C2(\unité_de_controle_1_rc2 ),
    .R_D2(\unité_de_controle_1_rd2 ));
  LED Fetch (.in(\unité_de_controle_1_fetch ));
  // Probe on banc_de_registre_1_out_1
  // Probe on banc_de_registre_1_out_2
  \Unité_de_controle  \unité_de_controle_1  (
    .Instruction(rom_1_data), .Clk(Clk_out), .PC_In(unite_adressage_1_pc_out), .Reset(Reset),
    .AD_Out(\unité_de_controle_1_ad_out ), .F0(\unité_de_controle_1_f0 [0]),
    .F1(\unité_de_controle_1_f0 [1]), .F2(\unité_de_controle_1_f0 [2]), .Load(\unité_de_controle_1_load ),
    .Store(\unité_de_controle_1_store ), .Fetch(\unité_de_controle_1_fetch ),
    .W_PC(\unité_de_controle_1_w_pc ), .W_AD(\unité_de_controle_1_w_ad ),
    .PC_Out(\unité_de_controle_1_pc_out ), .WA(\unité_de_controle_1_wa ), .WB(\unité_de_controle_1_wb ),
    .WC(\unité_de_controle_1_wc ), .WD(\unité_de_controle_1_wd ), .RA1(\unité_de_controle_1_ra1 ),
    .RA2(\unité_de_controle_1_ra2 ), .RB1(\unité_de_controle_1_rb1 ), .RB2(\unité_de_controle_1_rb2 ),
    .RC1(\unité_de_controle_1_rc1 ), .RC2(\unité_de_controle_1_rc2 ), .RD1(\unité_de_controle_1_rd1 ),
    .RD2(\unité_de_controle_1_rd2 ));  // open: Ext2, Ext1
  // Probe on \unité_de_controle_1_f0 
  ROM #(.addrWidth(4), .dataWidth(12)) rom_1 (.addr(unite_adressage_1_pc_out), .data(rom_1_data), .sel(1'b1));
  RAM #(.addrWidth(4), .dataWidth(4), .bus("separate")) ram_1 (
    .addr(unite_adressage_1_ad_out), .din(pull_resistor_1_node), .data(pull_resistor_2_node),
    .str(\unité_de_controle_1_store ), .sel(1'b1), .clk(Clk_out), .ld(\unité_de_controle_1_load ));  // open: clr
  ALU_4 alu_4_1 (
    .A(banc_de_registre_1_out_1), .B(banc_de_registre_1_out_2), .Sel(\unité_de_controle_1_f0 ),
    .S(pull_resistor_1_node), .Ret_Out(Ret_Out), .Z(Z_Out__1_si_Soustraction_0__0_sinon));
  // Probe on pull_resistor_2_node
  // Probe on pull_resistor_1_node
  Unite_Adressage unite_adressage_1 (
    .PC_In(\unité_de_controle_1_pc_out ), .W_PC(\unité_de_controle_1_w_pc ),
    .AD_In(\unité_de_controle_1_ad_out ), .W_AD(\unité_de_controle_1_w_ad ),
    .PC_Out(unite_adressage_1_pc_out), .AD_Out(unite_adressage_1_ad_out), .Clock(Clk_out), .Reset(Reset));
  // Probe on unite_adressage_1_ad_out

  // Notes on the sheet:
  //   contents of rom_1 (hex, n*v repeats v):
  //   400 444 5c4 8fc
endmodule
